// Logisim project T2 - EJ03.circ as structural Verilog: 1 circuit, main circuit main
module main (
  input  [5:0] in_1
);

  wire [1:0] \Opción ;
  wire [5:0] multiplexer_1_out, not_1_out, Resta, Suma;

  Adder #(.width(6)) adder_1 (.a(in_1), .b(6'b000011), .out(Suma), .cin(1'b0));  // open: cout
  Adder #(.width(6)) adder_2 (.a(in_1), .b(not_1_out), .out(Resta), .cin(1'b1));  // open: cout
  assign not_1_out = ~6'b000011;  // NOT_Gate not_1, 6 bits wide
  // Probe on multiplexer_1_out
  Multiplexer #(.select(2), .width(6), .disabled(0), .enable("false")) multiplexer_1 (
    .in0(Suma), .in1(Resta), .in2(in_1), .out(multiplexer_1_out), .sel(\Opción ));  // open: in3
  Comparator #(.width(6), .mode("unsigned")) comparator_1 (
    .a({1'b0, in_1[4:0]}), .b({in_1[5], {5{1'b0}}}), .gt(\Opción [0]), .eq(\Opción [1]));  // open: lt

  // Other names for the same wires on the sheet: X[5:0] = in_1
endmodule
