// Logisim project T2 - EJ04.circ as structural Verilog: 1 circuit, main circuit main
module main (
  input  [4:0] in_1,
  input  [3:0] in_2
);

  wire a_t, b_t, or_1_out;
  wire [5:0] S, xor_1_out, xor_6_out;

  xor xor_1 (xor_1_out[0], a_t, in_1[0]);
  xor xor_2 (xor_1_out[1], a_t, in_1[1]);
  xor xor_3 (xor_1_out[2], a_t, in_1[2]);
  xor xor_4 (xor_1_out[3], a_t, in_1[3]);
  xor xor_5 (xor_1_out[5], a_t, in_1[4]);
  xor xor_6 (xor_6_out[0], b_t, in_2[0]);
  xor xor_7 (xor_6_out[1], b_t, in_2[1]);
  xor xor_8 (xor_6_out[2], b_t, in_2[2]);
  xor xor_9 (xor_6_out[5], b_t, in_2[3]);
  // Probe on S
  Comparator #(.width(5), .mode("unsigned")) comparator_1 (
    .a({in_2[3], in_1[3:0]}), .b({in_1[4], in_2}), .gt(b_t), .lt(a_t));  // open: eq
  or or_1 (or_1_out, a_t, b_t);
  Adder #(.width(6)) adder_1 (
    .a({{2{xor_1_out[5]}}, xor_1_out[3:0]}), .b({{3{xor_6_out[5]}}, xor_6_out[2:0]}), .out(S), .cin(or_1_out));  // open: cout

  // Other names for the same wires on the sheet: A[4:0] = in_1; B[3:0] = in_2
endmodule
