// Logisim project T2 - EJ05.circ as structural Verilog: 1 circuit, main circuit main
module main (
  input  [3:0] in_1,
  input  [3:0] in_2
);

  wire [0:0] adder_3_out;
  wire [1:0] comparator_1_gt;
  wire [2:0] Valor_medio;
  wire [3:0] adder_1_out, adder_2_out, Distancia, not_1_out, not_2_out;

  assign not_1_out = ~in_2;  // NOT_Gate not_1, 4 bits wide
  Adder #(.width(4)) adder_1 (.a(in_2), .b(not_2_out), .out(adder_1_out), .cin(1'b1));  // open: cout
  assign not_2_out = ~in_1;  // NOT_Gate not_2, 4 bits wide
  Adder #(.width(4)) adder_2 (.a(in_1), .b(not_1_out), .out(adder_2_out), .cin(1'b1));  // open: cout
  // Probe on {2'b00, Valor_medio}
  // Probe on {2'b00, Valor_medio}
  // Probe on Distancia
  // Probe on Distancia
  Multiplexer #(.select(2), .width(4), .disabled(0), .enable("false")) multiplexer_1 (
    .in0(adder_2_out), .in1(adder_1_out), .in2(4'b0000), .out(Distancia), .sel(comparator_1_gt));  // open: in3
  Comparator #(.width(4), .mode("unsigned")) comparator_1 (
    .a(in_2), .b(in_1), .gt(comparator_1_gt[0]), .eq(comparator_1_gt[1]));  // open: lt
  // Probe on {Valor_medio, adder_3_out[0]}
  Adder #(.width(4)) adder_3 (.a(in_1), .b(in_2), .out({Valor_medio, adder_3_out[0]}));  // open: cin, cout
  // Probe on {Valor_medio, adder_3_out[0]}
  // Probe on {2'b00, Valor_medio}
  // Probe on {2'b00, Valor_medio}

  // Other names for the same wires on the sheet: A[3:0] = in_1; B[3:0] = in_2
endmodule
