// Logisim project T2 - EJ06.circ as structural Verilog: 1 circuit, main circuit main
module main (
  input  [1:0] in_1,
  input  [1:0] in_2
);

  wire multiplexer_1_out, not_1_out, or_1_out, xor_1_out, xor_2_out;

  xor xor_1 (xor_1_out, in_1[0], in_2[0]);
  xor xor_2 (xor_2_out, in_1[1], in_2[1]);
  or or_1 (or_1_out, xor_1_out, xor_2_out);
  Multiplexer #(.disabled(0), .enable("false")) multiplexer_1 (
    .in0(1'b0), .in1(not_1_out), .out(multiplexer_1_out), .sel(or_1_out));
  not not_1 (not_1_out, 1'b0);
  // Probe on multiplexer_1_out
endmodule
