// Logisim project T2 - EJ07.circ as structural Verilog: 1 circuit, main circuit main
module main (
  input  [3:0] in_1,
  input  [3:0] in_2
);

  wire [1:0] comparator_1_gt;
  wire [3:0] multiplexer_1_out;

  Comparator #(.width(4), .mode("unsigned")) comparator_1 (
    .a({in_2[3], in_1[2:0]}), .b({in_1[3], in_2[2:0]}), .gt(comparator_1_gt[0]), .eq(comparator_1_gt[1]));  // open: lt
  Multiplexer #(.select(2), .width(4), .disabled(0), .enable("false")) multiplexer_1 (
    .in0(in_2), .in1(in_1), .in2(in_1), .out(multiplexer_1_out), .sel(comparator_1_gt));  // open: in3
  // Probe on multiplexer_1_out

  // Other names for the same wires on the sheet: A[3:0] = in_1; B[3:0] = in_2
endmodule
