// Logisim project T2 - EJ10.circ as structural Verilog: 1 circuit, main circuit main
module main (
  input  [3:0] A,
  input  [3:0] B,
  input  [3:0] C
);

  wire [1:0] N;
  wire [2:0] comparator_1_eq;
  wire [3:0] S;

  // Probe on N
  // Probe on S
  Comparator #(.width(4), .mode("unsigned")) comparator_1 (.a(A), .b(B), .eq(comparator_1_eq[0]));  // open: gt, lt
  Comparator #(.width(4), .mode("unsigned")) comparator_2 (.a(B), .b(C), .eq(comparator_1_eq[1]));  // open: gt, lt
  Comparator #(.width(4), .mode("unsigned")) comparator_3 (.a(A), .b(C), .eq(comparator_1_eq[2]));  // open: gt, lt
  Multiplexer #(.select(4), .width(4), .disabled(0), .enable("false")) multiplexer_1 (
    .in1(A), .in2(B), .in3(4'b0000), .in4(A), .in5(4'b0000), .in6(4'b0000), .in7(A), .in8(4'b0000),
    .in9(4'b0000), .in10(4'b0000), .in11(4'b0000), .in12(4'b0000), .in13(4'b0000), .in14(4'b0000),
    .in15(4'b0000), .out(S), .sel({1'b0, comparator_1_eq}));  // open: in0
  // Probe on {1'b0, comparator_1_eq}
  Adder #(.width(1)) adder_1 (
    .a(comparator_1_eq[1]), .b(comparator_1_eq[2]), .out(N[0]), .cin(comparator_1_eq[0]), .cout(N[1]));
endmodule
