// Logisim project T2 - EJ11.circ as structural Verilog: 1 circuit, main circuit main
module main (
  input  [3:0] E
);

  wire [3:0] multiplexer_1_out, not_1_out;

  assign not_1_out = ~E;  // NOT_Gate not_1, 4 bits wide
  Multiplexer #(.select(4), .width(4), .disabled(0), .enable("false")) multiplexer_1 (
    .in0(not_1_out), .in1(not_1_out), .in2(not_1_out), .in3(not_1_out), .in4(not_1_out), .in5(not_1_out),
    .in6(not_1_out), .in7(not_1_out), .in8(4'b0000), .in9(4'b0000), .in10(4'b0000), .in11(4'b0000),
    .in12(4'b0100), .in13(4'b0100), .in14(4'b0100), .in15(4'b0100), .out(multiplexer_1_out), .sel(E));
  // Probe on multiplexer_1_out

  // Notes on the sheet:
  //   Ni idea de como hacerlo con codificadores y descodificadores
endmodule
