// Logisim project T3 - EJ06.circ as structural Verilog: 1 circuit, main circuit main
module main (
);

  wire CLK, comparator_1_eq, Forzar_entrada;
  wire [1:0] comparator_2_eq;
  wire [3:0] counter_1_q, counter_2_q, Entrada;

  Clock clock_1 (.out(CLK));
  Counter #(.width(4), .max('hf)) counter_1 (
    .Q(counter_1_q), .clk(CLK), .clr(comparator_1_eq));  // open: load, D, count, carry
  Comparator #(.width(4), .mode("unsigned")) comparator_1 (
    .a(counter_1_q), .b(4'b0111), .eq(comparator_1_eq));  // open: gt, lt
  // Probe on counter_2_q
  Counter #(.width(4), .max('hf)) counter_2 (
    .load(Forzar_entrada), .D(Entrada), .Q(counter_2_q), .clk(CLK));  // open: count, carry, clr
  Comparator #(.width(4), .mode("unsigned")) comparator_2 (
    .a(counter_2_q), .b(4'b0010), .eq(comparator_2_eq[0]));  // open: gt, lt
  Comparator #(.width(4), .mode("unsigned")) comparator_3 (
    .a(counter_2_q), .b(4'b1111), .eq(comparator_2_eq[1]));  // open: gt, lt
  or or_1 (Forzar_entrada, comparator_2_eq[0], comparator_2_eq[1]);
  Multiplexer #(.select(2), .width(4), .disabled(0), .enable("false")) multiplexer_1 (
    .in1(4'b1100), .in2(4'b0000), .out(Entrada), .sel(comparator_2_eq));  // open: in0, in3

  // Notes on the sheet:
  //   De 0 a 6
endmodule
