// Logisim project T2 - EJ02.circ as structural Verilog: 1 circuit, main circuit main
module main (
  input  [2:0] A,
  input  [3:0] B
);

  wire [3:0] adder_1_out;
  wire [4:0] adder_2_out;

  // Probe on B
  // Probe on {1'b0, A}
  // Probe on adder_1_out
  Adder #(.width(4)) adder_1 (.a({1'b0, A}), .b(B), .out(adder_1_out));  // open: cin, cout
  // Probe on {3'b000, B[3:2]}
  Adder #(.width(5)) adder_2 (.a({1'b0, adder_1_out}), .b({3'b000, B[3:2]}), .out(adder_2_out));  // open: cin, cout
  // Probe on adder_2_out
endmodule
