// Logisim project T2 - EJ08.circ as structural Verilog: 1 circuit, main circuit main
module main (
  input  in_1,
  input  [3:0] in_2,
  input  in_3,
  input  [3:0] in_4,
  input  in_5,
  input  [3:0] in_6,
  input  in_7,
  input  [3:0] in_8,
  input  in_9
);

  wire Aa, Ab, Ac, Ad, priority_encoder_1_en_out, priority_encoder_1_gs;
  wire [1:0] priority_encoder_1_out;
  wire [3:0] Y;

  // Probe on priority_encoder_1_en_out
  Priority_Encoder #(.select(2), .disabled(0)) priority_encoder_1 (
    .in0(in_1), .in1(in_3), .in2(in_5), .in3(in_7), .out(priority_encoder_1_out), .gs(priority_encoder_1_gs),
    .en_out(priority_encoder_1_en_out), .en_in(in_9));
  // Probe on priority_encoder_1_gs
  // Probe on Y
  Multiplexer #(.select(2), .width(4), .disabled(0), .enable("false")) multiplexer_1 (
    .in0(in_2), .in1(in_4), .in2(in_6), .in3(in_8), .out(Y), .sel(priority_encoder_1_out));
  Decoder #(.select(2), .disabled(0), .enable("false")) decoder_1 (
    .out0(Ad), .out1(Ac), .out2(Ab), .out3(Aa), .sel(priority_encoder_1_out));
  // Probe on Ad
  // Probe on Ac
  // Probe on Ab
  // Probe on Aa

  // Other names for the same wires on the sheet: Da[3:0] = in_8; Db[3:0] = in_6; Dc[3:0] = in_4; Dd[3:0] = in_2;
  //   Ra = in_7; Rb = in_5; Rc = in_3; Rd = in_1
endmodule
