// Logisim project T3 - EJ07.circ as structural Verilog: 1 circuit, main circuit main
module main (
  input  [3:0] in_1,
  input  [3:0] in_2,
  input  in_3
);

  wire CLK, comparator_1_eq, comparator_2_lt, comparator_3_eq, comparator_4_eq, not_1_out, or_1_out,
       or_2_out, Valor_para_empezar;
  wire [3:0] multiplexer_1_out, multiplexer_2_out, Valor_si_X_Y, Valor_si_X_Y_t;

  Clock clock_1 (.out(CLK));
  Counter #(.width(4), .max('hf)) counter_1 (
    .load(comparator_1_eq), .D(in_1), .Q(Valor_si_X_Y), .clk(CLK));  // open: count, carry, clr
  // Probe on in_1
  // Probe on in_2
  // Probe on Valor_si_X_Y
  Multiplexer #(.width(4), .disabled(0), .enable("false")) multiplexer_1 (
    .in0(in_1), .in1(4'b0000), .out(multiplexer_1_out), .sel(Valor_para_empezar));
  Comparator #(.width(4), .mode("unsigned")) comparator_1 (
    .a(Valor_si_X_Y), .b(in_2), .eq(comparator_1_eq));  // open: gt, lt
  not not_1 (not_1_out, Valor_para_empezar);
  or or_1 (or_1_out, not_1_out, comparator_3_eq);
  Counter #(.width(4), .max('hf)) counter_2 (
    .load(or_1_out), .D(multiplexer_1_out), .Q(Valor_si_X_Y_t), .clk(CLK), .clr(in_3));  // open: count, carry
  Comparator #(.width(4), .mode("unsigned")) comparator_2 (.a(in_1), .b(in_2), .lt(comparator_2_lt));  // open: gt, eq
  Comparator #(.width(4), .mode("unsigned")) comparator_3 (
    .a(Valor_si_X_Y_t), .b(in_2), .eq(comparator_3_eq));  // open: gt, lt
  Multiplexer #(.width(4), .disabled(0), .enable("false")) multiplexer_2 (
    .in0(Valor_si_X_Y_t), .in1(Valor_si_X_Y), .out(multiplexer_2_out), .sel(comparator_2_lt));
  Comparator #(.width(4), .mode("unsigned")) comparator_4 (
    .a(Valor_si_X_Y_t), .b(in_1), .eq(comparator_4_eq));  // open: gt, lt
  // Probe on multiplexer_2_out
  or or_2 (or_2_out, Valor_para_empezar, comparator_4_eq);
  Register #(.width(1)) register_1 (.D(or_2_out), .Q(Valor_para_empezar), .clk(CLK), .clr(in_3));  // open: en
  // NAND_Gate nand_1 is placed but not wired

  // Other names for the same wires on the sheet: R = in_3; X[3:0] = in_1; Y[3:0] = in_2

  // Notes on the sheet:
  //   Importante dejar R a 0 cuando haga un reset
endmodule
